# Fritzing sketch EMBEDDED-SD-PROJ (saved by Fritzing 0.9.3b)
breadboards: 1

parts:
  Microcontroller = Arduino Uno (Rev3) - ICSP
  BUZZER = Piezo Speaker
  12V_POWER_SUPPLY = DC Power [voltage=5]
  IRF520_MOSFET = IFR520 MOS module [package=THT]
  POTENTIOMETER = POT [package=pot_mammoth]
  LED_LIGHT = LED - 5mm [color="Red (633nm)" package="5 mm [THT]"]
  M1 = RioRand LM2596

nets:
  N1: Microcontroller.A0, POTENTIOMETER.S
  N2: Microcontroller.5V, POTENTIOMETER.A
  GND: Microcontroller.GND, BUZZER.pin2, IRF520_MOSFET.GND, POTENTIOMETER.E, M1.Pin_4
  N3: Microcontroller.D3_PWM, IRF520_MOSFET.SIG
  N4: Microcontroller.D4, BUZZER.pin1
  N5: 12V_POWER_SUPPLY.V+, M1.Pin_1
  N6: 12V_POWER_SUPPLY.V-, M1.Pin_2
  N7: IRF520_MOSFET.V+, LED_LIGHT.anode
  N8: IRF520_MOSFET.V-, LED_LIGHT.cathode
  N9: IRF520_MOSFET.VIN, M1.Pin_3
