# Fritzing sketch schematicDiagram (saved by Fritzing 0.9.3b)
breadboards: 1

parts:
  Microcontroller = Arduino Uno (Rev3) - ICSP
  BUZZER = Piezo Speaker
  12V_POWER_SUPPLY = DC Power [voltage=5]
  IRF520_MOSFET = IFR520 MOS module [package=THT]
  POTENTIOMETER = POT [package=pot_mammoth]
  LED_LIGHT = LED - 5mm [color="Red (633nm)" current=0.030 package="5 mm [THT]"]
  M1 = RioRand LM2596
  Part1 = Adafruit DS1307 RTC Breakout [part_number="Adafruit #264"]

nets:
  N1: Microcontroller.A0, POTENTIOMETER.S
  N2: Microcontroller.5V, POTENTIOMETER.A
  GND: Microcontroller.GND, BUZZER.pin2, 12V_POWER_SUPPLY.V-, IRF520_MOSFET.GND, POTENTIOMETER.E, M1.Pin_2, M1.Pin_4, Part1.GND
  N3: Microcontroller.D2, Part1.SQW
  N4: Microcontroller.D3_PWM, Part1.SCL
  N5: Microcontroller.D4, Part1.SDA
  N6: Microcontroller.D5_PWM, IRF520_MOSFET.SIG
  N7: Microcontroller.D6_PWM, BUZZER.pin1
  VIN: Microcontroller.VIN, 12V_POWER_SUPPLY.V+, M1.Pin_1, Part1.VCC
  N8: IRF520_MOSFET.V+, LED_LIGHT.anode
  N9: IRF520_MOSFET.V-, LED_LIGHT.cathode
  N10: IRF520_MOSFET.VIN, M1.Pin_3

custom parts:
  Adafruit DS1307 RTC Breakout: This is a great battery-backed real time clock (RTC) that allows your microcontroller project to keep track of time even if it is reprogrammed, or if the power is lost. Perfect for datalogging, clock-building, time stamping, timers and alarms, etc. The DS1307 is the most popular RTC - but it requires 5V power to work (although we've used it with 5V power and 3.3V logic successfully) PCB &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
